# Fritzing sketch AeroGuard Breadboard circuit 04-15-2026 (saved by Fritzing 1.0.6)
breadboards: 1

parts:
  AITRIP_ESP32-C3_OLED_dev = ESP32-C3 0.42in OLED
  mini_vibration_motor = Vibration Motor- ROB-08449 [package=vibe-motor-10mm]
  3_7_V_LiPo_250mAh_battery = LIPO-110mAh [package=lipo-110]
  HiLetgo_TP4056_battery_charger_module = TP4056 [chip_label=TP4056 package="DIP (Dual Inline) [THT]"]
  OLED_screen = Grove OLED 128x96
  JACK1 = 2.1mm Barrel Jack with Terminal Block
  Power_supply = Power Jack [package=power_jack_smd]
  Sensor = BME680 Module [part_number=BME680]
  NPN_Transistor_PN2222 = TRANSISTOR_NPN [package=to-92-ammo]
  Resistor = Resistor [tolerance=±5% resistance=220 package="0805 [SMD]"]
  R1 = Resistor [tolerance=±5% power=0.25W resistance=10k package=THT]
  R2 = Resistor [tolerance=±5% power=0.25W resistance=10k package=THT]
  Button = SWITCH-MOMENTARY-2 [package=tactile_switch_smd]  # not connected
  Flyback_Diode = Diode [package=diode-1n4001]

nets:
  N1: AITRIP_ESP32-C3_OLED_dev.Pin_2, R1.Pin_0, R2.Pin_0
  N2: AITRIP_ESP32-C3_OLED_dev.Pin_3, Resistor.Pin_1
  N3: AITRIP_ESP32-C3_OLED_dev.Pin_4, OLED_screen.SDA, Sensor.SDA
  N4: AITRIP_ESP32-C3_OLED_dev.Pin_5, OLED_screen.SCL, Sensor.SCL
  5V: AITRIP_ESP32-C3_OLED_dev.Pin_9, mini_vibration_motor.-, HiLetgo_TP4056_battery_charger_module.pin3, Flyback_Diode.C
  GND: AITRIP_ESP32-C3_OLED_dev.Pin_10, 3_7_V_LiPo_250mAh_battery.-, HiLetgo_TP4056_battery_charger_module.pin5, HiLetgo_TP4056_battery_charger_module.pin6, OLED_screen.GND, Sensor.GND, NPN_Transistor_PN2222.E, R1.Pin_1
  3.3V: AITRIP_ESP32-C3_OLED_dev.Pin_11, OLED_screen.VCC, Sensor.VCC
  N5: mini_vibration_motor.+, NPN_Transistor_PN2222.C, Flyback_Diode.A
  N6: 3_7_V_LiPo_250mAh_battery.+, HiLetgo_TP4056_battery_charger_module.pin4, R2.Pin_1
  N7: HiLetgo_TP4056_battery_charger_module.pin1, JACK1.POS, Power_supply.PWR
  N8: HiLetgo_TP4056_battery_charger_module.pin2, JACK1.NEG, Power_supply.GND
  N9: NPN_Transistor_PN2222.B, Resistor.Pin_0

notes:
  Equivalent LiPo battery but the real battery has 250 mAh
  This will be a USB Type-C cable in reality
  Our OLED screen's pin layout is:
  SDA, SCL, GND, VCC
  so the real breadboarding will be slightly different. SDA for the BME680 sensor and the OLED screen will be connected to GPIO pin 6. SCL for the BME680 sensor and the OLED screen will be connected to GPIO pin 7.

custom parts:
  ESP32-C3 0.42in OLED: ESP32-C3 0.42-Inch Oled White Light Display Bluetooth Development Board Type-C.
  TP4056: A DIP stand-in part for whatever IC you want. With 6 pins on a 300mil dual inline package (DIP) footprint.
  BME680 Module: Bosch BME680 Development Module The BME680 is a digital 4-in-1 sensor that measures air quality [gas], humidity, pressure and temperature. Links: BME680 product datasheet
